# Fritzing sketch Arduino-Light Source Switch (saved by Fritzing 0.9.3b)
circuit board: 3.5cm x 4cm

parts:
  Composant1 = Arduino Nano (Rev3.0)  # not connected
  J10 = female pin header, 15 pins [form="♀ (female)"]
  J11 = female pin header, 15 pins [form="♀ (female)"]
  S1 = Round Pushbutton
  R1 = Resistor [tolerance=±5% resistance=2.2k package=THT]
  R2 = Resistor [tolerance=±5% resistance=220 package=THT]
  LED2 = LED - 5mm [color="Green (560nm)" package="5 mm [THT]"]
  LED1 = LED - 5mm [color="Red (633nm)" package="5 mm [THT]"]
  J12 = Dagu DGServo 9g header connector (female) [package=THT]
  J13 = Basic Servo  # not connected

nets:
  N1: J10.pin2, J12.gnd
  N2: J10.pin4, S1.leg0, J12.Vcc
  N3: J11.pin4, R1.Pin_1
  N4: J11.pin5, S1.leg1, R1.Pin_0
  N5: J11.pin7, R2.Pin_0
  N6: J11.pin8, LED2.cathode, LED1.anode
  N7: J11.pin9, J12.pulse
  N8: R2.Pin_1, LED2.anode, LED1.cathode
